// Logisim project Task-2.circ as structural Verilog: 1 circuit, main circuit main
module main (
  input  A,
  input  B,
  output out_3
);

  wire nor_1_out, nor_2_out, nor_3_out, nor_4_out;

  nor nor_1 (nor_1_out, A, A);
  nor nor_2 (nor_2_out, B, B);
  nor nor_3 (nor_3_out, A, B);
  nor nor_4 (nor_4_out, nor_1_out, nor_2_out);
  nor nor_5 (out_3, nor_4_out, nor_3_out);

  // Notes on the sheet:
  //   XOR using NOR
endmodule
