// Logisim project Lab-3.1.circ as structural Verilog: 1 circuit, main circuit main
module main (
  input  A,
  input  B,
  input  C,
  output out_4
);

  wire ic_7404_1_p6, ic_7404_1_p7, ic_7404_1_p8, ic_7404_1_p9, ic_7404_1_p10, ic_7411_1_p3, ic_7411_1_p4,
       ic_7411_1_p5;

  // IC_7404 ic_7404_1: pin names not known; wires that end beside it: A, B, A, C, C, ic_7404_1_p6, ic_7404_1_p7, ic_7404_1_p8, ic_7404_1_p9, ic_7404_1_p10, C, ic_7404_1_p8, B, ic_7404_1_p9, A, B, ic_7404_1_p10
  // IC_7411 ic_7411_1: pin names not known; wires that end beside it: ic_7404_1_p6, ic_7404_1_p7, ic_7411_1_p3, ic_7411_1_p4, ic_7411_1_p5
  // IC4075_main main_1: pin names not known; wires that end beside it: ic_7411_1_p3, ic_7411_1_p4, ic_7411_1_p5, out_4

  // Notes on the sheet:
  //   1st Canonical form
  //   F = A'B'C+A'BC'+ABC'
endmodule
