// Logisim project Lab-3.2.circ as structural Verilog: 1 circuit, main circuit main
module main (
  input  A,
  input  B,
  input  C,
  output out_4
);

  wire ic_7404_1_p6, ic_7404_1_p7, ic_7404_1_p8, main_1_p9, main_1_p10, main_1_p11, main_2_p7, main_2_p8;

  // IC_7404 ic_7404_1: pin names not known; wires that end beside it: B, C, B, C, A, ic_7404_1_p6, ic_7404_1_p7, ic_7404_1_p8, C
  // IC4075_main main_1: pin names not known; wires that end beside it: A, B, C, A, ic_7404_1_p6, ic_7404_1_p7, ic_7404_1_p8, B, main_1_p9, main_1_p10, main_1_p11
  // IC4075_main main_2: pin names not known; wires that end beside it: ic_7404_1_p8, B, ic_7404_1_p7, ic_7404_1_p8, ic_7404_1_p6, ic_7404_1_p7, main_2_p7, main_2_p8
  // IC_7411 ic_7411_1: pin names not known; wires that end beside it: main_1_p9, main_1_p10, main_1_p11, out_4, main_2_p7, main_2_p8, out_4

  // Notes on the sheet:
  //   2nd canonical form
  //   F=(A+B+C)(A+B'+C')(A'+B+C)(A'+B+C')(A'+B'+C')
endmodule
